# Fritzing sketch schematic (saved by Fritzing 0.9.3b)
breadboards: 1

parts:
  Part1 = Arduino Uno (Rev3)
  R1 = Resistor [tolerance=±5% resistance=330 package=THT]
  R2 = Resistor [tolerance=±5% resistance=330 package=THT]
  R4 = Trimmer Potentiometer [maximum_resistance=10kΩ package=THT]
  LED1 = LED - 5mm [color="Red (633nm)" package="5 mm [THT]"]
  LED2 = LED - 5mm [color="Red (633nm)" package="5 mm [THT]"]
  LED4 = LED - 5mm [color="Red (633nm)" package="5 mm [THT]"]
  R5 = Resistor [tolerance=±5% resistance=330 package=THT]

nets:
  N1: Part1.D11_PWM/MOSI, R1.Pin_0
  N2: Part1.D12/MISO, R2.Pin_0
  N3: Part1.D13/SCK, R5.Pin_0
  N4: Part1.GND, R4.leg1, LED1.cathode, LED2.cathode, LED4.cathode
  N5: R1.Pin_1, R4.leg2
  N6: R2.Pin_1, LED1.anode
  N7: R4.wiper, LED4.anode
  N8: LED2.anode, R5.Pin_1
