# Fritzing sketch digital-pwm (saved by Fritzing 0.9.2b)
breadboards: 1

parts:
  Part1 = Arduino Uno (Rev3)
  R1 = Resistor [tolerance=±5% resistance=330 package=THT]
  R2 = Rotary Potentiometer (Small) [maximum_resistance=100kΩ package=THT]
  R3 = Resistor [tolerance=±5% resistance=10k package=THT]
  LED1 = LED - 5mm [color="Red (633nm)" package="5 mm [THT]"]

nets:
  N1: Part1.A0, R2.wiper
  N2: Part1.D12/MISO, R1.Pin_0
  N3: Part1.GND, R2.leg2, LED1.cathode
  N4: Part1.5V, R3.Pin_0
  N5: R1.Pin_1, LED1.anode
  N6: R2.leg1, R3.Pin_1
